# Fritzing sketch SmartAutomaticGearbox (saved by Fritzing 0.9.6b)
circuit board: 7cm x 2.8cm

parts:
  J1 = female pin header, 12 pins [form="♀ (female)"]
  J2 = female pin header, 12 pins [form="♀ (female)"]
  J3 = female pin header, 4 pins [form="♀ (female)"]
  SN65HVD23O = SN65HVD230 CAN Bus transciever module [package=THT]
  MP1584EN = MP1584EN Power Regulator Board [part_number=MP1584EN]
  LD2 = LED - 3mm [color="Green (570nm)" current=0.030 package="3 mm [THT]"]
  LD1 = LED - 3mm [color="Red (633nm)" current=0.030 package="3 mm [THT]"]
  1K = Resistor [tolerance=±5% resistance=1k power=0.25 package=THT]

nets:
  N1: J1.pin1, MP1584EN.OUT_+
  N2: J1.pin12, SN65HVD23O.pin_1
  N3: J2.pin1, 1K.Pin_1
  N4: J2.pin2, MP1584EN.OUT_-
  N5: J2.pin4, LD2.cathode
  N6: J2.pin5, LD1.cathode
  N7: J2.pin6, SN65HVD23O.pin_3
  N8: J2.pin9, SN65HVD23O.pin_4
  N9: J2.pin11, SN65HVD23O.pin_2
  N10: J3.pin1, SN65HVD23O.pin_5
  N11: J3.pin2, SN65HVD23O.pin_6
  N12: J3.pin3, MP1584EN.IN_-
  N13: J3.pin4, MP1584EN.IN_+
  N14: LD2.anode, LD1.anode, 1K.Pin_0

notes:
  Tx
  Smart Automatic
  INT-OUT
  3V3
  36
  37
  38
  39
  32
  33
  25
  26
  27
  GND
  5V
  17
  22
  15
  13
  2
  12
  21
  ESP32 TTGO T-DISPLAY
  OBD2
  6
  14
  4-5
  8
  Gearbox
  02/2023 -Jpnos

custom parts:
  SN65HVD230 CAN Bus transciever module: Bus Transceiver SN65HVD230 CAN Communication Module, for Arduino.
  MP1584EN Power Regulator Board: The MP1584EN is a high frequency step-down switching regulator. The input voltage range is 4.5V to 28V. The output voltage is set by the board's potentiometer.
